# Fritzing sketch voltage_controller (saved by Fritzing 0.9.3b)
breadboards: 1

parts:
  Part1 = Arduino Mega 2560 (Rev3)
  Part2 = Tri-Axis Gyro Breakout - L3G4200D  # not connected
  Q1 = Basic FET P-Channel [package="TO220 [THT]"]
  D1 = Rectifier Diode [part_number=1N4001 package="300 mil [THT]"]
  D2 = Rectifier Diode [part_number=1N4001 package="300 mil [THT]"]  # not connected
  LED1 = LED - 5mm [color="Red (633nm)" package="5 mm [THT]"]
  Power_plug1 = Power plug

nets:
  N1: Part1.D9_PWM, Q1.gate
  N2: Part1.5V, Q1.source
  GND: Part1.GND, D1.anode, Power_plug1.GND
  N3: Q1.drain, D1.cathode, LED1.cathode
  N4: LED1.anode, Power_plug1.VCC
