# Fritzing sketch voltage_gyro_controller (saved by Fritzing 0.9.3b)
breadboards: 2

parts:
  Part1 = Arduino Mega 2560 (Rev3)
  Q1 = Basic FET P-Channel [package="TO220 [THT]"]
  D1 = Rectifier Diode [part_number=1N4001 package="300 mil [THT]"]
  D2 = Rectifier Diode [part_number=1N4001 package="300 mil [THT]"]  # not connected
  LED1 = LED - 5mm [color="Red (633nm)" package="5 mm [THT]"]
  Power_plug1 = Power plug
  Part3 = Triple Axis Gyro Breakout ITG-3200

nets:
  N1: Part1.D21/SCL, Part3.SCL
  N2: Part1.D20/SDA, Part3.SDA
  N3: Part1.D9_PWM, Q1.gate
  3V3: Part1.3V3, Part3.VCC, Part3.VLOGIC
  N4: Part1.5V, Q1.source
  GND: Part1.GND, D1.anode, Power_plug1.GND, Part3.GND
  N5: Q1.drain, D1.cathode, LED1.cathode
  N6: LED1.anode, Power_plug1.VCC
